// Logisim project AdderSubtractor.circ as structural Verilog: 12 circuits, main circuit main
module main (
  input  [7:0] A,
  input  [7:0] B,
  output [7:0] Result,
  output out_4,
  output out_5,
  output out_6,
  output out_7,
  output out_8,
  output out_9,
  output out_10,
  output out_11
);

  wire addersubtractor_1_info, button_1_out, button_2_out, button_3_out, button_4_out, button_5_out,
       button_6_out, clock_1_out;

  Button button_1 (.out(button_1_out));
  Button button_2 (.out(button_2_out));
  Button button_3 (.out(button_3_out));
  Button button_4 (.out(button_4_out));
  Button button_5 (.out(button_5_out));
  Button button_6 (.out(button_6_out));
  Clock clock_1 (.out(clock_1_out));
  AdderSubtractor addersubtractor_1 (
    .A(A), .B(B), .InitialState(button_1_out), .StateReset(button_2_out), .InputLoad(button_3_out),
    .InputReset(button_4_out), .Add(button_5_out), .Subtract(button_6_out), .Clk(clock_1_out),
    .Info(addersubtractor_1_info), .Result({out_4, out_5, out_6, out_7, out_8, out_9, out_10, out_11}));
  LED led_1 (.in(addersubtractor_1_info));

  assign Result = {out_4, out_5, out_6, out_7, out_8, out_9, out_10, out_11};

  // Notes on the sheet:
  //   ON
  //   OFF
  //   Load Input
  //   Clear
  //   Add
  //   Subtract
  //   ON / OFF
  //   State information : x = 1
  //   OUTPUT
endmodule

module FullAdder (
  input  X,
  input  Y,
  input  Cin,
  output Sum,
  output Cout
);

  wire and_1_out, and_2_out, xor_1_out;

  xor xor_1 (xor_1_out, X, Y);
  xor xor_2 (Sum, xor_1_out, Cin);
  and and_1 (and_1_out, Cin, xor_1_out);
  and and_2 (and_2_out, X, Y);
  or or_1 (Cout, and_1_out, and_2_out);
endmodule

module FullAdder8Bit (
  input  [7:0] X7toX0,
  input  [7:0] Y7toY0,
  input  Cin,
  output [7:0] R7toR0,
  output Cout
);

  wire fulladder_2_cout, fulladder_3_cout, fulladder_4_cout, fulladder_5_cout, fulladder_6_cout,
       fulladder_7_cout, fulladder_8_cout;

  FullAdder fulladder_1 (.X(X7toX0[7]), .Y(Y7toY0[7]), .Cin(fulladder_2_cout), .Sum(R7toR0[7]), .Cout(Cout));
  FullAdder fulladder_2 (
    .X(X7toX0[6]), .Y(Y7toY0[6]), .Cin(fulladder_3_cout), .Sum(R7toR0[6]), .Cout(fulladder_2_cout));
  FullAdder fulladder_3 (
    .X(X7toX0[5]), .Y(Y7toY0[5]), .Cin(fulladder_4_cout), .Sum(R7toR0[5]), .Cout(fulladder_3_cout));
  FullAdder fulladder_4 (
    .X(X7toX0[4]), .Y(Y7toY0[4]), .Cin(fulladder_5_cout), .Sum(R7toR0[4]), .Cout(fulladder_4_cout));
  FullAdder fulladder_5 (
    .X(X7toX0[3]), .Y(Y7toY0[3]), .Cin(fulladder_6_cout), .Sum(R7toR0[3]), .Cout(fulladder_5_cout));
  FullAdder fulladder_6 (
    .X(X7toX0[2]), .Y(Y7toY0[2]), .Cin(fulladder_7_cout), .Sum(R7toR0[2]), .Cout(fulladder_6_cout));
  FullAdder fulladder_7 (
    .X(X7toX0[1]), .Y(Y7toY0[1]), .Cin(fulladder_8_cout), .Sum(R7toR0[1]), .Cout(fulladder_7_cout));
  FullAdder fulladder_8 (.X(X7toX0[0]), .Y(Y7toY0[0]), .Cin(Cin), .Sum(R7toR0[0]), .Cout(fulladder_8_cout));

  // Notes on the sheet:
  //   8-bit Y
  //   RESULT
  //   8-bit X
endmodule

module ArithmeticCircuit (
  input  [7:0] X7toX0,
  input  [7:0] Y7toY0,
  input  Cin,
  input  [1:0] S1S0,
  output [7:0] R,
  output Cout
);

  wire [7:0] and_1_out, and_2_out, bit_extender_1_out, bit_extender_2_out, not_1_out, or_1_out;

  assign not_1_out = ~Y7toY0;  // NOT_Gate not_1, 8 bits wide
  assign bit_extender_1_out = {{7{S1S0[0]}}, S1S0[0]};  // Bit_Extender bit_extender_1
  assign bit_extender_2_out = {{7{S1S0[1]}}, S1S0[1]};  // Bit_Extender bit_extender_2
  assign and_1_out = bit_extender_1_out & Y7toY0;  // AND_Gate and_1, 8 bits wide
  assign and_2_out = bit_extender_2_out & not_1_out;  // AND_Gate and_2, 8 bits wide
  assign or_1_out = and_1_out | and_2_out;  // OR_Gate or_1, 8 bits wide
  FullAdder8Bit fulladder8bit_1 (.X7toX0(X7toX0), .Y7toY0(or_1_out), .Cin(Cin), .R7toR0(R), .Cout(Cout));

  // Notes on the sheet:
  //   X
  //   Y
  //   Selections
  //   Selections
  //   S1S0
  //   00: Y -> 0
  //   01: Y -> Y
  //   10: Y -> Y'
  //   11: Y -> 1
  //   Selections
  //   Selections
  //   S1 S0 Cin
  //   000: R = X
  //   001: R = X + 1
  //   010: R = X + Y
  //   110: R = X - 1
  //   111: R = X
  //   011: R = X + Y + 1
  //   100: R = X + Y' = A - B - 1
  //   101: R = X + Y' + 1 = A - B
  //   RESULT
  //   RESULT
endmodule

module LogicCircuit (
  input  [7:0] A7toA0,
  input  [7:0] B7toB0,
  input  [1:0] S1S0,
  output [7:0] R
);

  wire [7:0] and_1_out, not_1_out, or_1_out, xor_1_out;

  assign or_1_out = B7toB0 | A7toA0;  // OR_Gate or_1, 8 bits wide
  assign xor_1_out = B7toB0 ^ A7toA0;  // XOR_Gate xor_1, 8 bits wide
  assign and_1_out = B7toB0 & A7toA0;  // AND_Gate and_1, 8 bits wide
  assign not_1_out = ~A7toA0;  // NOT_Gate not_1, 8 bits wide
  Multiplexer #(.select(2), .width(8), .enable("false")) multiplexer_1 (
    .in0(or_1_out), .in1(xor_1_out), .in2(and_1_out), .in3(not_1_out), .out(R), .sel(S1S0));

  // Notes on the sheet:
  //   8-bit A
  //   8-bit B
  //   Selections
  //   Selections
  //   S1S0
  //   00: AND
  //   01: OR
  //   10: NOT
  //   11: XOR
  //   RESULT
  //   RESULT
endmodule

module ALUCircuit (
  input  [7:0] A7toA0,
  input  [7:0] B7toB0,
  input  Cin,
  input  [2:0] S2S1S0,
  output [7:0] O7toO0,
  output Cout
);

  wire [7:0] arithmeticcircuit_1_r, logiccircuit_1_r;

  ArithmeticCircuit arithmeticcircuit_1 (
    .X7toX0(A7toA0), .Y7toY0(B7toB0), .Cin(Cin), .S1S0(S2S1S0[1:0]), .R(arithmeticcircuit_1_r), .Cout(Cout));
  LogicCircuit logiccircuit_1 (.A7toA0(A7toA0), .B7toB0(B7toB0), .S1S0(S2S1S0[1:0]), .R(logiccircuit_1_r));
  Multiplexer #(.width(8), .enable("false")) multiplexer_1 (
    .in0(arithmeticcircuit_1_r), .in1(logiccircuit_1_r), .out(O7toO0), .sel(S2S1S0[2]));

  // Notes on the sheet:
  //   A
  //   B
  //   Selections
  //   Selections
  //   S2S1S0
  //   100: OR
  //   101: XOR
  //   110: AND
  //   111: NOT
  //   RESULT
  //   RESULT
  //   R
  //   R
  //   S2 S1 S0 Cin
  //   0000: R = A
  //   0001: R = A + 1
  //   0010: R = A + B
  //   0101: R =  A - B
  //   0110: R = A - 1
  //   0111: R = A
  //   0011: R = A + B + 1
  //   0100: R = A + B' = A - B - 1
  //   100X: R = A AND B
  //   101X: R = A XOR B
  //   110X: R = A AND B
  //   111X: R = A' (NOT)
endmodule

module Register1Bit (
  input  I,
  input  Load,
  input  Reset,
  input  Clk,
  output O
);

  wire multiplexer_1_out;

  Multiplexer #(.enable("false")) multiplexer_1 (.in0(O), .in1(I), .out(multiplexer_1_out), .sel(Load));
  D_Flip_Flop d_ff_1 (.D(multiplexer_1_out), .clk(Clk), .Q(O), .preset(1'b0), .reset(Reset));  // open: Qn

  // Notes on the sheet:
  //   Set operation
  //   not required
  //   Input
  //   Ouput
endmodule

module Register8Bit (
  input  [7:0] I7toI0,
  input  Load,
  input  Reset,
  input  Clk,
  output [7:0] O7toO0
);

  wire multiplexer_1_out, multiplexer_2_out, multiplexer_3_out, multiplexer_4_out, multiplexer_5_out,
       multiplexer_6_out, multiplexer_7_out, multiplexer_8_out;

  Multiplexer #(.enable("false")) multiplexer_1 (.in0(O7toO0[0]), .in1(I7toI0[0]), .out(multiplexer_1_out), .sel(Load));
  Multiplexer #(.enable("false")) multiplexer_2 (.in0(O7toO0[1]), .in1(I7toI0[1]), .out(multiplexer_2_out), .sel(Load));
  Multiplexer #(.enable("false")) multiplexer_3 (.in0(O7toO0[2]), .in1(I7toI0[2]), .out(multiplexer_3_out), .sel(Load));
  Multiplexer #(.enable("false")) multiplexer_4 (.in0(O7toO0[3]), .in1(I7toI0[3]), .out(multiplexer_4_out), .sel(Load));
  Multiplexer #(.enable("false")) multiplexer_5 (.in0(O7toO0[4]), .in1(I7toI0[4]), .out(multiplexer_5_out), .sel(Load));
  Multiplexer #(.enable("false")) multiplexer_6 (.in0(O7toO0[5]), .in1(I7toI0[5]), .out(multiplexer_6_out), .sel(Load));
  Multiplexer #(.enable("false")) multiplexer_7 (.in0(O7toO0[6]), .in1(I7toI0[6]), .out(multiplexer_7_out), .sel(Load));
  Multiplexer #(.enable("false")) multiplexer_8 (.in0(O7toO0[7]), .in1(I7toI0[7]), .out(multiplexer_8_out), .sel(Load));
  D_Flip_Flop d_ff_1 (.D(multiplexer_1_out), .clk(Clk), .Q(O7toO0[0]), .preset(1'b0), .reset(Reset));  // open: Qn
  D_Flip_Flop d_ff_2 (.D(multiplexer_2_out), .clk(Clk), .Q(O7toO0[1]), .preset(1'b0), .reset(Reset));  // open: Qn
  D_Flip_Flop d_ff_3 (.D(multiplexer_3_out), .clk(Clk), .Q(O7toO0[2]), .preset(1'b0), .reset(Reset));  // open: Qn
  D_Flip_Flop d_ff_4 (.D(multiplexer_4_out), .clk(Clk), .Q(O7toO0[3]), .preset(1'b0), .reset(Reset));  // open: Qn
  D_Flip_Flop d_ff_5 (.D(multiplexer_5_out), .clk(Clk), .Q(O7toO0[4]), .preset(1'b0), .reset(Reset));  // open: Qn
  D_Flip_Flop d_ff_6 (.D(multiplexer_6_out), .clk(Clk), .Q(O7toO0[5]), .preset(1'b0), .reset(Reset));  // open: Qn
  D_Flip_Flop d_ff_7 (.D(multiplexer_7_out), .clk(Clk), .Q(O7toO0[6]), .preset(1'b0), .reset(Reset));  // open: Qn
  D_Flip_Flop d_ff_8 (.D(multiplexer_8_out), .clk(Clk), .Q(O7toO0[7]), .preset(1'b0), .reset(Reset));  // open: Qn

  // Notes on the sheet:
  //   8-bit I
  //   8-bit O
endmodule

module OptionalInverter (
  input  I,
  input  En,
  output O
);

  wire xor_1_out;

  xor xor_1 (xor_1_out, I, 1'b1);
  Multiplexer #(.enable("false")) multiplexer_1 (.in0(I), .in1(xor_1_out), .out(O), .sel(En));

  // Notes on the sheet:
  //   Input
  //   Input XOR 1
  //   No change
  //   I -> I'
  //   If Enable = '1'
  //   I -> I'
  //   Output
endmodule

module SignBitOperator (
  input  A,
  input  B,
  input  InputSelect,
  input  InvertSelect,
  output R,
  output Load
);

  wire multiplexer_1_out;

  Multiplexer #(.enable("false")) multiplexer_1 (.in0(A), .in1(B), .out(multiplexer_1_out), .sel(InputSelect));
  or or_1 (Load, InputSelect, InvertSelect);
  OptionalInverter optionalinverter_1 (.I(multiplexer_1_out), .En(InvertSelect), .O(R));
endmodule

module ControlUnit (
  input  Start,
  input  Reset,
  input  S,
  input  qa,
  input  qs,
  input  E,
  input  Clk,
  output Z,
  output Y,
  output X,
  output Cin,
  output S2,
  output S1,
  output S0,
  output L
);

  wire and_1_out, and_2_out, and_3_out, and_4_out, and_5_out, and_6_out, and_7_out, FF2_q, FF3_q, FF4_q,
       FF5_q, or_1_out, or_2_out;

  and and_1 (and_1_out, ~qa, ~qs, X);  // AND_Gate
  or or_1 (or_1_out, and_1_out, and_6_out, FF3_q, Z);
  D_Flip_Flop FF0 (.D(or_1_out), .clk(Clk), .Q(X), .preset(Start), .reset(Reset));  // open: Qn
  and and_2 (and_2_out, X, qs);
  D_Flip_Flop FF1 (.D(and_2_out), .clk(Clk), .Q(Y), .preset(1'b0), .reset(Reset));  // open: Qn
  or or_2 (or_2_out, Y, and_3_out);
  and and_3 (and_3_out, X, qa);
  D_Flip_Flop FF2 (.D(or_2_out), .clk(Clk), .Q(FF2_q), .preset(1'b0), .reset(Reset));  // open: Qn
  or or_3 (S0, FF3_q, S2);
  and and_4 (and_4_out, FF2_q, ~S);  // AND_Gate
  D_Flip_Flop FF3 (.D(and_4_out), .clk(Clk), .Q(FF3_q), .preset(1'b0), .reset(Reset));  // open: Qn
  and and_5 (and_5_out, FF2_q, S);
  D_Flip_Flop FF4 (.D(and_5_out), .clk(Clk), .Q(FF4_q), .preset(1'b0), .reset(Reset));  // open: Qn
  or or_4 (S1, FF4_q, S2);
  or or_5 (Cin, FF4_q, Z);
  and and_6 (and_6_out, E, FF5_q);
  D_Flip_Flop FF5 (.D(FF4_q), .clk(Clk), .Q(FF5_q), .preset(1'b0), .reset(Reset));  // open: Qn
  and and_7 (and_7_out, FF5_q, ~E);  // AND_Gate
  D_Flip_Flop FF6 (.D(and_7_out), .clk(Clk), .Q(S2), .preset(1'b0), .reset(Reset));  // open: Qn
  or or_6 (L, FF3_q, FF4_q, S2, Z);
  D_Flip_Flop FF7 (.D(S2), .clk(Clk), .Q(Z), .preset(1'b0), .reset(Reset));  // open: Qn

  // Notes on the sheet:
  //   qa
  //   qs
  //   T0
  //   qa'qs'T0
  //   T5*E
  //   T3
  //   T7
  //   T0
  //   T0
  //   qs
  //   T0*qs
  //   T0
  //   T1
  //   T1
  //   qa
  //   T2
  //   T0*qa
  //   T3+T6
  //   S
  //   T2*S'
  //   T2
  //   T2*S
  //   T4+T6
  //   E
  //   S
  //   T4+T7
  //   T5
  //   T5*E
  //   E
  //   T5
  //   T5*E'
  //   T3+T4+T6+T7
  //   T6
  //   As != Bs
  //   ADD
  //   SUBTRACT
  //   Cout
  //   T7
  //   Not
  //   Required
  //   Set
endmodule

module AdderSubtractor (
  input  [7:0] A,
  input  [7:0] B,
  input  InitialState,
  input  StateReset,
  input  InputLoad,
  input  InputReset,
  input  Add,
  input  Subtract,
  input  Clk,
  output Info,
  output [7:0] Result
);

  wire alucircuit_1_cout, controlunit_1_cin, controlunit_1_l, controlunit_1_y, controlunit_1_z, or_1_out,
       or_2_out, register1bit_2_o, register1bit_3_o, signbitoperator_1_load, signbitoperator_1_r,
       signbitoperator_2_load, signbitoperator_2_r, xor_1_out;
  wire [2:0] controlunit_1_s0;
  wire [6:0] multiplexer_1_out, multiplexer_2_out;
  wire [7:0] alucircuit_1_o7too0, register8bit_2_o7too0;
  wire [7:7] register8bit_1_o7too0;

  Multiplexer #(.width(7), .enable("false")) multiplexer_1 (
    .in0(alucircuit_1_o7too0[6:0]), .in1(A[6:0]), .out(multiplexer_1_out), .sel(InputLoad));
  Multiplexer #(.width(7), .enable("false")) multiplexer_2 (
    .in0(register8bit_2_o7too0[6:0]), .in1(B[6:0]), .out(multiplexer_2_out), .sel(InputLoad));
  SignBitOperator signbitoperator_1 (
    .A(Result[7]), .B(A[7]), .InputSelect(InputLoad), .InvertSelect(controlunit_1_z),
    .R(signbitoperator_1_r), .Load(signbitoperator_1_load));
  SignBitOperator signbitoperator_2 (
    .A(register1bit_2_o), .B(B[7]), .InputSelect(InputLoad), .InvertSelect(controlunit_1_y),
    .R(signbitoperator_2_r), .Load(signbitoperator_2_load));
  Register1Bit register1bit_1 (
    .I(signbitoperator_1_r), .Load(signbitoperator_1_load), .Reset(InputReset), .Clk(Clk), .O(Result[7]));
  Register1Bit register1bit_2 (
    .I(signbitoperator_2_r), .Load(signbitoperator_2_load), .Reset(InputReset), .Clk(Clk),
    .O(register1bit_2_o));
  xor xor_1 (xor_1_out, register1bit_2_o, Result[7]);
  ControlUnit controlunit_1 (
    .Start(InitialState), .Reset(StateReset), .S(xor_1_out), .qa(Add), .qs(Subtract), .E(register1bit_3_o),
    .Clk(Clk), .Z(controlunit_1_z), .Y(controlunit_1_y), .X(Info), .Cin(controlunit_1_cin),
    .S2(controlunit_1_s0[2]), .S1(controlunit_1_s0[1]), .S0(controlunit_1_s0[0]), .L(controlunit_1_l));
  or or_1 (or_1_out, InputLoad, controlunit_1_l);
  or or_2 (or_2_out, Info, InputReset);
  Register8Bit register8bit_1 (
    .I7toI0({1'b0, multiplexer_1_out}), .Load(or_1_out), .Reset(InputReset), .Clk(Clk),
    .O7toO0({register8bit_1_o7too0[7], Result[6:0]}));
  Register8Bit register8bit_2 (
    .I7toI0({1'b0, multiplexer_2_out}), .Load(or_1_out), .Reset(InputReset), .Clk(Clk),
    .O7toO0(register8bit_2_o7too0));
  ALUCircuit alucircuit_1 (
    .A7toA0({register8bit_1_o7too0[7], Result[6:0]}), .B7toB0(register8bit_2_o7too0),
    .Cin(controlunit_1_cin), .S2S1S0(controlunit_1_s0), .O7toO0(alucircuit_1_o7too0), .Cout(alucircuit_1_cout));
  Register1Bit register1bit_3 (
    .I(alucircuit_1_cout), .Load(controlunit_1_l), .Reset(or_2_out), .Clk(Clk), .O(register1bit_3_o));

  // Notes on the sheet:
  //   As : Bs
  //   is it equal?
  //   fill zero to sign bit
  //   InputLoad + L
  //   X + InputReset
  //   only take value bits
  //   As
endmodule
